// Logisim project diagram.circ as structural Verilog: 23 circuits, main circuit main
module main (
);

  wire and_1_out, controller_1_alusrca, controller_1_memread, controller_1_memtoreg, controller_1_memwrite,
       controller_1_mult_sign, controller_1_output_branch, controller_1_regdst, controller_1_regwrite,
       controller_1_se_ze, controller_1_start_mult, equalcomparator_1_eq, multiplier_1_s,
       pipeline_regde_1_alusrce, pipeline_regde_1_branche, pipeline_regde_1_memreade,
       pipeline_regde_1_memtorege, pipeline_regde_1_memwritee, pipeline_regde_1_mult_signe,
       pipeline_regde_1_regdste, pipeline_regde_1_regdste_2, pipeline_regde_1_regwrited_2,
       pipeline_regem_1_branchm, pipeline_regem_1_memtoregm, pipeline_regem_1_memwritem,
       pipeline_regem_1_mult_resultm, pipeline_regem_1_regwritem, pipeline_regmw_1_p10, pipeline_regmw_1_p11,
       pipeline_regmw_1_p14;
  wire [1:0] controller_1_out_select, pipeline_regde_1_out_selecte, pipeline_regem_1_out_selectm,
       pipeline_regmw_1_p12;
  wire [3:0] controller_1_alu_op, pipeline_regde_1_alucontrole;
  wire [4:0] multiplexer_1_out, pipeline_regde_1_rdd_2, pipeline_regde_1_rtd_2, pipeline_regem_1_writeregm,
       pipeline_regmw_1_p17;
  wire [25:0] pipeline_regfd_1_instrd;
  wire [27:0] leftshift2_26bit_1_out;
  wire [31:0] adder_1_s, adder_2_s, alu_1_aluout, data_memory_1_read_data, inst_memory_1_read_data,
       leftshift2_32bit_1_out, lui_extend_1_signextended, mux_alu_input_1_out, mux_branch_1_pcd,
       mux_jump_1_pcd, mux_memtoreg_1_out, mux_outselect_1_out, pc_1_pcf, pipeline_regde_1_pc_4e,
       pipeline_regde_1_rf_readdata1_e, pipeline_regde_1_rf_readdata2_e, pipeline_regde_1_signimme,
       pipeline_regem_1_aluoutm, pipeline_regem_1_pc_4m, pipeline_regem_1_write_datam,
       pipeline_regfd_1_pcplusd, pipeline_regmw_1_p13, pipeline_regmw_1_p15, pipeline_regmw_1_p16,
       reg_file_1_rd1, reg_file_1_rd2, signextend_1_signextended, undriven;
  wire [31:26] pipeline_regfd_1_instrd_2;

  EqualComparator equalcomparator_1 (.a(undriven), .b({32{1'b0}}), .eq(equalcomparator_1_eq));
  and and_1 (and_1_out, equalcomparator_1_eq, pipeline_regem_1_branchm);
  MUX_BRANCH mux_branch_1 (
    .PC_4(adder_1_s), .Branch_Addr(pipeline_regem_1_pc_4m), .PCD(mux_branch_1_pcd), .Se_ze(and_1_out));
  LeftShift2_26bit leftshift2_26bit_1 (.in(pipeline_regfd_1_instrd), .out(leftshift2_26bit_1_out));
  MUX_JUMP mux_jump_1 (
    .ImmShift2({4'b0000, leftshift2_26bit_1_out}), .PC_4(mux_branch_1_pcd), .PCD(mux_jump_1_pcd),
    .Se_ze(controller_1_se_ze));
  PC pc_1 (.PC(mux_jump_1_pcd), .PCF(pc_1_pcf));  // open: CLK, EN
  Inst_memory inst_memory_1 (.address(pc_1_pcf), .Read_data(inst_memory_1_read_data));
  Adder adder_1 (.a(pc_1_pcf), .b(32'h4), .S(adder_1_s));
  Pipeline_RegFD pipeline_regfd_1 (
    .InstrF(inst_memory_1_read_data), .PCPlus4F(adder_1_s),
    .InstrD({pipeline_regfd_1_instrd_2, pipeline_regfd_1_instrd}), .PCPlusD(pipeline_regfd_1_pcplusd));  // open: Clk, EN, CLR
  Reg_file reg_file_1 (
    .PR1(pipeline_regfd_1_instrd[25:21]), .PR2(pipeline_regfd_1_instrd[20:16]), .WR(pipeline_regmw_1_p17),
    .WD(mux_outselect_1_out), .RD1(reg_file_1_rd1), .RD2(reg_file_1_rd2), .Write(pipeline_regmw_1_p10));  // open: Reset, Clk
  controller controller_1 (
    .op(pipeline_regfd_1_instrd_2), .Func(pipeline_regfd_1_instrd[5:0]), .MemRead(controller_1_memread),
    .MemWrite(controller_1_memwrite), .RegWrite(controller_1_regwrite), .ALUSrcA(controller_1_alusrca),
    .se_ze(controller_1_se_ze), .RegDst(controller_1_regdst), .start_mult(controller_1_start_mult),
    .mult_sign(controller_1_mult_sign), .MemtoReg(controller_1_memtoreg),
    .Out_select(controller_1_out_select), .ALU_op(controller_1_alu_op),
    .Output_branch(controller_1_output_branch));  // open: Eq_ne, PC_source, ALUSrcB
  SignExtend signextend_1 (.Input(pipeline_regfd_1_instrd[15:0]), .SignExtended(signextend_1_signextended));
  Pipeline_RegDE pipeline_regde_1 (
    .RegWriteD(controller_1_regwrite), .MemtoRegD(controller_1_memtoreg), .MemWriteD(controller_1_memwrite),
    .ALUControlD(controller_1_alu_op), .ALUSrcD(controller_1_alusrca), .RegDstD(controller_1_regdst),
    .BranchD(controller_1_output_branch), .RsD(pipeline_regfd_1_instrd[25:21]),
    .RtD(pipeline_regfd_1_instrd[20:16]), .RtD_2(pipeline_regde_1_rtd_2),
    .RdD(pipeline_regfd_1_instrd[15:11]), .RdD_2(pipeline_regde_1_rdd_2),
    .SignImmD(signextend_1_signextended), .PC_4D(pipeline_regfd_1_pcplusd),
    .RegWriteD_2(pipeline_regde_1_regwrited_2), .MemtoRegE(pipeline_regde_1_memtorege),
    .MemWriteE(pipeline_regde_1_memwritee), .ALUControlE(pipeline_regde_1_alucontrole),
    .ALUSrcE(pipeline_regde_1_alusrce), .RegDstE_2(pipeline_regde_1_regdste_2),
    .BranchE(pipeline_regde_1_branche), .RF_ReadData1_D(reg_file_1_rd1),
    .RF_ReadData1_E(pipeline_regde_1_rf_readdata1_e), .RF_ReadData2_D(reg_file_1_rd2),
    .RF_ReadData2_E(pipeline_regde_1_rf_readdata2_e), .SignImmE(pipeline_regde_1_signimme),
    .PC_4E(pipeline_regde_1_pc_4e), .MemReadD(controller_1_memread), .MemReadE(pipeline_regde_1_memreade),
    .start_multD(controller_1_start_mult), .RegDstE(pipeline_regde_1_regdste),
    .Out_selectD(controller_1_out_select), .Out_selectE(pipeline_regde_1_out_selecte),
    .mult_signD(controller_1_mult_sign), .mult_signE(pipeline_regde_1_mult_signe));  // open: RsD_2, Clk, CLR
  Multiplier multiplier_1 (
    .a(pipeline_regde_1_rf_readdata1_e), .s(multiplier_1_s), .start(pipeline_regde_1_regdste),
    .Is_signed(pipeline_regde_1_mult_signe), .b(pipeline_regde_1_rf_readdata2_e));  // open: Clk
  Multiplexer #(.width(5), .enable("false")) multiplexer_1 (
    .in0(pipeline_regde_1_rtd_2), .in1(pipeline_regde_1_rdd_2), .out(multiplexer_1_out),
    .sel(pipeline_regde_1_regdste_2));
  MUX_ALU_Input mux_alu_input_1 (
    .RF_ReadData2(pipeline_regde_1_rf_readdata2_e), .SignedImm(pipeline_regde_1_signimme),
    .Out(mux_alu_input_1_out), .ALUSrc(pipeline_regde_1_alusrce));
  LeftShift2_32bit leftshift2_32bit_1 (.in(pipeline_regde_1_signimme), .out(leftshift2_32bit_1_out));
  ALU alu_1 (
    .In1(pipeline_regde_1_rf_readdata1_e), .In2(mux_alu_input_1_out), .ALUout(alu_1_aluout),
    .Func(pipeline_regde_1_alucontrole));
  Adder adder_2 (.a(leftshift2_32bit_1_out), .b(pipeline_regde_1_pc_4e), .S(adder_2_s));
  Pipeline_RegEM pipeline_regem_1 (
    .MemReadE(pipeline_regde_1_memreade), .RegWriteE(pipeline_regde_1_regwrited_2),
    .MemtoRegE(pipeline_regde_1_memtorege), .MemWriteE(pipeline_regde_1_memwritee),
    .BranchE(pipeline_regde_1_branche), .Out_selectE(pipeline_regde_1_out_selecte),
    .WriteRegE(multiplexer_1_out), .WriteRegM(pipeline_regem_1_writeregm), .PC_4E(adder_2_s),
    .RegWriteM(pipeline_regem_1_regwritem), .MemtoRegM(pipeline_regem_1_memtoregm),
    .MemWriteM(pipeline_regem_1_memwritem), .BranchM(pipeline_regem_1_branchm),
    .Out_selectM(pipeline_regem_1_out_selectm), .ALUoutE(alu_1_aluout), .ALUoutM(pipeline_regem_1_aluoutm),
    .write_dataE(undriven), .write_dataM(pipeline_regem_1_write_datam), .PC_4M(pipeline_regem_1_pc_4m),
    .mult_resultE(multiplier_1_s), .mult_resultM(pipeline_regem_1_mult_resultm));  // open: MemReadM, Clk
  lui_extend lui_extend_1 (.Input(pipeline_regem_1_aluoutm), .SignExtended(lui_extend_1_signextended));
  Data_memory data_memory_1 (
    .address(pipeline_regem_1_aluoutm), .Write(pipeline_regem_1_memwritem),
    .Read_data(data_memory_1_read_data));  // open: write_data, Clk
  // Pipeline_RegMW pipeline_regmw_1: pin names not known; wires that end beside it: pipeline_regem_1_regwritem, pipeline_regem_1_memtoregm, pipeline_regem_1_out_selectm, pipeline_regem_1_aluoutm, pipeline_regem_1_mult_resultm, data_memory_1_read_data, pipeline_regem_1_write_datam, lui_extend_1_signextended, pipeline_regem_1_writeregm, pipeline_regmw_1_p10, pipeline_regmw_1_p11, pipeline_regmw_1_p12, pipeline_regmw_1_p13, pipeline_regmw_1_p14, pipeline_regmw_1_p15, pipeline_regmw_1_p16, pipeline_regmw_1_p17
  MUX_MemtoReg mux_memtoreg_1 (
    .ALUout(pipeline_regmw_1_p13), .ReadData(pipeline_regmw_1_p15), .out(mux_memtoreg_1_out),
    .MemtoReg(pipeline_regmw_1_p11));
  MUX_OutSelect mux_outselect_1 (
    .Out_select(pipeline_regmw_1_p12), .ALUout(mux_memtoreg_1_out), .mult_result_high(pipeline_regmw_1_p14),
    .out(mux_outselect_1_out), .mult_result_low(pipeline_regmw_1_p14), .lui_extend(pipeline_regmw_1_p16));
endmodule

module controller (
  input  [5:0] op,
  input  [5:0] Func,
  input  Eq_ne,
  input  PC_source,
  output se_ze,
  output ALUSrcB,
  output mult_sign,
  output MemRead,
  output RegWrite,
  output MemtoReg,
  output MemWrite,
  output [3:0] ALU_op,
  output ALUSrcA,
  output start_mult,
  output RegDst,
  output Output_branch,
  output [1:0] Out_select
);
endmodule

module ALU (
  input  [31:0] In1,
  input  [31:0] In2,
  input  [3:0] Func,
  output [31:0] ALUout
);
endmodule

module Data_memory (
  input  Clk,
  input  Write,
  input  [31:0] address,
  input  [31:0] write_data,
  output [31:0] Read_data
);
endmodule

module Inst_memory (
  input  [31:0] address,
  output [31:0] Read_data
);
endmodule

module Reg_file (
  input  Clk,
  input  Write,
  input  Reset,
  input  [4:0] PR1,
  input  [4:0] PR2,
  input  [4:0] WR,
  input  [31:0] WD,
  output [31:0] RD1,
  output [31:0] RD2
);
endmodule

module Multiplier (
  input  [31:0] a,
  input  [31:0] b,
  input  Clk,
  input  start,
  input  Is_signed,
  output s
);
endmodule

module EqualComparator (
  input  [31:0] a,
  input  [31:0] b,
  output eq
);
endmodule

module Adder (
  input  [31:0] a,
  input  [31:0] b,
  output [31:0] S
);
endmodule

module PC (
  input  CLK,
  input  [31:0] PC,
  input  EN,
  output [31:0] PCF
);
endmodule

module MUX_JUMP (
  input  Se_ze,
  input  [31:0] PC_4,
  input  [31:0] ImmShift2,
  output [31:0] PCD
);
endmodule

module MUX_BRANCH (
  input  Se_ze,
  input  [31:0] PC_4,
  input  [31:0] Branch_Addr,
  output [31:0] PCD
);
endmodule

module MUX_ALU_Input (
  input  ALUSrc,
  input  [31:0] RF_ReadData2,
  input  [31:0] SignedImm,
  output [31:0] Out
);
endmodule

module MUX_OutSelect (
  input  [1:0] Out_select,
  input  [31:0] ALUout,
  input  mult_result_high,
  input  mult_result_low,
  input  [31:0] lui_extend,
  output [31:0] out
);
endmodule

module MUX_MemtoReg (
  input  MemtoReg,
  input  [31:0] ALUout,
  input  [31:0] ReadData,
  output [31:0] out
);
endmodule

module Pipeline_RegFD (
  input  Clk,
  input  [31:0] InstrF,
  input  [31:0] PCPlus4F,
  input  EN,
  input  CLR,
  output [31:0] InstrD,
  output [31:0] PCPlusD
);
endmodule

module Pipeline_RegDE (
  input  Clk,
  input  mult_signD,
  input  MemReadD,
  input  RegWriteD,
  input  MemtoRegD,
  input  MemWriteD,
  input  [3:0] ALUControlD,
  input  ALUSrcD,
  input  start_multD,
  input  RegDstD,
  input  BranchD,
  input  [1:0] Out_selectD,
  input  [31:0] RF_ReadData1_D,
  input  [31:0] RF_ReadData2_D,
  input  [4:0] RsD,
  input  [4:0] RtD,
  input  [4:0] RdD,
  input  [31:0] SignImmD,
  input  [31:0] PC_4D,
  input  CLR,
  output mult_signE,
  output MemReadE,
  output RegWriteD_2,
  output MemtoRegE,
  output MemWriteE,
  output [3:0] ALUControlE,
  output ALUSrcE,
  output RegDstE,
  output RegDstE_2,
  output BranchE,
  output [1:0] Out_selectE,
  output [31:0] RF_ReadData1_E,
  output [31:0] RF_ReadData2_E,
  output [4:0] RsD_2,
  output [4:0] RtD_2,
  output [4:0] RdD_2,
  output [31:0] SignImmE,
  output [31:0] PC_4E
);
endmodule

module Pipeline_RegEM (
  input  Clk,
  input  MemReadE,
  input  RegWriteE,
  input  MemtoRegE,
  input  MemWriteE,
  input  BranchE,
  input  [1:0] Out_selectE,
  input  [31:0] ALUoutE,
  input  mult_resultE,
  input  [31:0] write_dataE,
  input  [4:0] WriteRegE,
  input  [31:0] PC_4E,
  output MemReadM,
  output RegWriteM,
  output MemtoRegM,
  output MemWriteM,
  output BranchM,
  output [1:0] Out_selectM,
  output [31:0] ALUoutM,
  output mult_resultM,
  output [31:0] write_dataM,
  output [4:0] WriteRegM,
  output [31:0] PC_4M
);
endmodule

module Pipeline_RegMW (
  input  Clk,
  input  RegWriteM,
  input  MemtoRegM,
  input  [1:0] Out_selectM,
  input  mult_resultM,
  input  [31:0] lui_resultM,
  input  [31:0] ReadDataM,
  input  [31:0] ALUoutM,
  input  [4:0] WriteRegM,
  output RegWriteW,
  output MemtoRegW,
  output [1:0] Out_selectW,
  output mult_resultW,
  output [31:0] lui_resultW,
  output [31:0] ReadDataW,
  output [31:0] ALUoutW,
  output [4:0] WriteRegW
);
endmodule

module SignExtend (
  input  [15:0] Input,
  output [31:0] SignExtended
);
endmodule

module LeftShift2_32bit (
  input  [31:0] in,
  output [31:0] out
);
endmodule

module LeftShift2_26bit (
  input  [25:0] in,
  output [27:0] out
);
endmodule

module lui_extend (
  input  [31:0] Input,
  output [31:0] SignExtended
);
endmodule
